# Fritzing sketch Project_Veroboard_Sketch (saved by Fritzing 0.9.3b)
stripboards: 1

parts:
  IC1 = IC, DIP package, 28 pins [chip_label=IC]
  JP1 = Header 1 [package=1x01_offset]
  JP2 = Header 1 [package=1x01_offset]
  JP3 = Header 1 [package=1x01_offset]
  JP4 = Header 1 [package=1x01_offset]
  JP5 = Header 1 [package=1x01_offset]
  R1 = Resistor [tolerance=±5% resistance=10k package="0402 [SMD]"]
  C1 = Tantalum Capacitor [capacitance=10µF package="D 7343 [SMD, tantalum]"]
  JP6 = Header 1 [package=1x01_offset]
  JP7 = Header 1 [package=1x01_offset]  # not connected
  JP8 = Header 1 [package=1x01_offset]
  JP9 = Header 1 [package=1x01_offset]
  JP10 = Header 1 [package=1x01_offset]  # not connected
  JP11 = Header 1 [package=1x01_offset]  # not connected
  JP12 = Header 1 [package=1x01_offset]
  JP13 = Header 1 [package=1x01_offset]
  IC2 = V_REG_LD1117VXX [package=78xxl]
  C2 = Tantalum Capacitor [capacitance=10µF package="D 7343 [SMD, tantalum]"]
  C3 = Tantalum Capacitor [capacitance=10µF package="D 7343 [SMD, tantalum]"]
  JP14 = Header 1 [package=1x01_offset]
  JP15 = Header 1 [package=1x01_offset]
  C4 = Tantalum Capacitor [capacitance=10µF package="D 7343 [SMD, tantalum]"]
  R2 = Temperature Sensor (Thermistor) [thermistor_type=NTC package=THT]
  R3 = Temperature Sensor (Thermistor) [thermistor_type=NTC package=THT]
  R4 = Resistor [tolerance=±5% resistance=1k package=THT]
  R5 = Resistor [tolerance=±5% resistance=1k package=THT]
  S1 = Round Pushbutton
  C5 = Tantalum Capacitor [capacitance=10µF package="D 7343 [SMD, tantalum]"]

nets:
  N1: IC1.pin1, IC1.pin8, IC1.pin19, IC1.pin27, JP1.1, JP3.1, R1.Pin_0, R1.Pin_1, C1.-, JP13.1, IC2.IN, C2.-, C3.-, JP15.1, C4.-, R4.Pin_1, R5.Pin_1, C5.-
  N2: IC1.pin2, R2.pin_1, R5.Pin_0
  N3: IC1.pin3, R3.pin_1, R4.Pin_0
  N4: IC1.pin4, JP4.1
  N5: IC1.pin5, JP5.1
  N6: IC1.pin13, IC1.pin23, IC1.pin28, JP2.1, JP6.1, JP8.1, C4.+, R2.pin_0, R3.pin_0, C5.+
  N7: IC1.pin17, JP9.1
  N8: IC1.pin18, JP12.1
  N9: IC1.pin20, C1.+
  N10: IC2.OUT, C3.+
  N11: IC2.GND, C2.+, JP14.1, S1.leg0, S1.leg1
